# Fritzing sketch RobotArmsRace_I2C (saved by Fritzing 0.9.0b)
breadboards: 1

parts:
  Raspberry_Pi_B_rev1 = Raspberry Pi B rev1
  U1 = MCP23017 [package=dip]

nets:
  3V3: Raspberry_Pi_B_rev1.3V3, U1.VDD, U1.RESET
  N1: Raspberry_Pi_B_rev1.GPIO_0, U1.SDA
  N2: Raspberry_Pi_B_rev1.GPIO_1, U1.SCL
  GND: Raspberry_Pi_B_rev1.GND, U1.VSS, U1.A0, U1.GPA7, U1.A2

notes:
  A0
  A1
  B0
  B1

custom parts:
  MCP23017: 16-Bit I/O Expander with Serial Interface
